# Fritzing sketch circuit (saved by Fritzing 0.9.2b)
breadboards: 1

parts:
  Composant2 = Arduino Xbee Libellium Shield
  U1 = XBee
  TMP36 = TMP36 Temperature Sensor [package="TO92 [THT]"]
  TMP36_2 = TMP36 Temperature Sensor [package="TO92 [THT]"]
  PIR_MOTION_SENSOR = PIR sensor
  Composant1 = Arduino Mega 2560 (Rev3)
  DS18B20 = TMP36 Temperature Sensor [package="TO92 [THT]"]
  Photorésistance = Photocell (LDR) [package=THT]
  R1 = Resistor [tolerance=±5% resistance=4.7k package="2010 [SMD]"]
  R2 = Resistor [tolerance=±5% resistance=220 package="2512 [SMD]"]

nets:
  N1: Composant2.M8RXD, Composant1.D0_RX0
  N2: Composant2.M8TXD, Composant1.D1_TX0, DS18B20.Vout, R1.Pin_1
  N3: Composant2.D2, Composant1.D2_PWM
  N4: Composant2.D3, Composant1.D3_PWM
  N5: Composant2.D4, Composant1.D4_PWM
  N6: Composant2.D5, Composant1.D5_PWM
  N7: Composant2.D6, Composant1.D6_PWM
  N8: Composant2.D7, Composant1.D7_PWM
  N9: Composant2.I/08, U1.pin20
  N10: Composant2.I/02, U1.pin19
  N11: Composant2.I/03, U1.pin18
  N12: Composant2.I/06, U1.pin17
  N13: Composant2.I/05, U1.pin16
  N14: Composant2.15, U1.pin15
  N15: Composant2.14, U1.pin14
  N16: Composant2.13, U1.pin13
  N17: Composant2.I/07, U1.pin12
  N18: Composant2.I/04, U1.pin11
  N19: Composant2.A5, Composant1.A5
  N20: Composant2.A4, Composant1.A4
  N21: Composant2.A3, Composant1.A3
  N22: Composant2.A2, Composant1.A2
  N23: Composant2.A1, Composant1.A1
  N24: Composant2.A0, Composant1.A0
  GND: Composant2.GND, U1.GND
  N25: Composant2.9, U1.pin9
  N26: Composant2.8, U1.pin8
  N27: Composant2.PWM1, U1.pin7
  N28: Composant2.PWM0, U1.pin6
  N29: Composant2.RST, U1.pin5
  N30: Composant2.4, U1.pin4
  N31: Composant2.DIN, U1.pin3
  N32: Composant2.DOUT, U1.pin2
  +3V3: Composant2.+3V3, U1.VCC
  VDD: TMP36.+Vs, TMP36_2.+Vs, PIR_MOTION_SENSOR.VDD, Composant1.5V, Photorésistance.pin_1, R1.Pin_0
  N33: TMP36.Vout, Composant1.A10
  GND_2: TMP36.GND, TMP36_2.GND, PIR_MOTION_SENSOR.GND, Composant1.GND, DS18B20.+Vs, DS18B20.GND, R2.Pin_0
  N34: TMP36_2.Vout, Composant1.A11
  N35: PIR_MOTION_SENSOR.SIG, Composant1.A12
  N36: Composant1.A7, Photorésistance.pin_0, R2.Pin_1

// code stored in the sketch: ALL.ino

// Ajouts des librairies


  //DS18B20 libs

  #include <OneWire.h>

  #include <DallasTemperature.h>

  //Xbee lib

  #include <SoftwareSerial.h>



// Xbee PIN

  #define RXPIN 0

  #define TXPIN 1

// Xbee Init

  SoftwareSerial XBeeSerial =  SoftwareSerial(RXPIN, TXPIN);



// fréquence

  #define BAUDRATE 9600



// Data wire is plugged into port 2 on the Arduino

  #define ONE_WIRE_BUS 2

// Setup a oneWire instance to communicate with any OneWire devices (not just Maxim/Dallas temperature ICs)

  OneWire oneWire(ONE_WIRE_BUS);

// Pass our oneWire reference to Dallas Temperature. 

  DallasTemperature sensors(&oneWire);





// Détecteur de présence

  int ledPin = 13;                // Pin de la LED

  int inputPin = 15;               // Pin d'entrée du PIR

  int pirState = LOW;             // we start, assuming no motion detected

  int val = 0;                    // variable for reading the pin status



// Photorésistance

  int photocellPin = 7; // the cell and 10K pulldown are connected to a0

  int photocellReading; // the analog reading from the analog resistor divider

//the time we give the sensor to calibrate (10-60 secs according to the datasheet)

  int calibrationTime = 10;



/*

 * The setup function.

 */

void setup(void)

{

  pinMode(ledPin, OUTPUT);      // LED as output

  pinMode(inputPin, INPUT);     // PIR sensor as input

  

  // Calibrate sensor for detect movement.

    //Serial.print("calibrating sensor ");

    for(int i = 0; i < calibrationTime; i++){ // see CalibrationTime var.

      delay(1000);

    }

  

  // start serial port

    Serial.begin(BAUDRATE);

    Serial.println("[INFOS] Arduino 1 ok.");

 

    // Envois un message aux modules xbee

    XBeeSerial.begin(BAUDRATE);

    XBeeSerial.println("[INFOS] Arduino 1 ok.");



  // Start up the library

    sensors.begin();

}



/*

 * Main function.

 */

void loop(void)

{ 

  /*----------------------------------------------------

   *                 PIR MOVEMENT SENSOR

   ---------------------------------------------------*/

    val = digitalRead(inputPin);  // There is someone?

    Serial.print("PIR(True/False) : ");Serial.println(val); // print result

    

    if (val == HIGH) { // check if the input is HIGH

      digitalWrite(ledPin, HIGH);  // turn LED ON

      delay(150);



      if (pirState == LOW) {

        // we have just turned on

        Serial.println("PIR - INFOS : Motion detected!");

        // We only want to print on the output change, not state

        pirState = HIGH;

      }

    } else {

      digitalWrite(ledPin, LOW); // turn LED OFF

      delay(300);

      

      if (pirState == HIGH){

        // we have just turned of

        Serial.println("PIR - INFOS : Motion ended!");

        // We only want to print on the output change, not state

        pirState = LOW;

      }

    }





  /*----------------------------------------------------

   *                 D18B20 SENSOR

   ---------------------------------------------------*/

    // call sensors.requestTemperatures() to issue a global temperature 

    // request to all devices on the bus

    //Serial.print("Requesting temperatures...");

    sensors.requestTemperatures(); // Send the command to get temperatures

    //Serial.println("DONE");

    // After we got the temperatures, we can print them here.

    // We use the function ByIndex, and as an example get the temperature from the first sensor only.

    Serial.print("DS18B20 : ");

    Serial.println(sensors.getTempCByIndex(0));  





  /*----------------------------------------------------

   *                 TMP36 SENSOR

   ---------------------------------------------------*/  

    int chaleurIntPin = 10;

    int inTmp36 = analogRead(chaleurIntPin);

    // 5/1023

      float temperatureC = ((inTmp36*0.004882) - 0.50) * 100 ;

    Serial.print("TMP36 : ");Serial.println(temperatureC);



  /*----------------------------------------------------

   *                 PHOTOCELL SENSOR

   ---------------------------------------------------*/

    photocellReading = analogRead(photocellPin);

    Serial.print("Analog reading = ");

    Serial.print(photocellReading); // the raw analog reading

    // We'll have a few threshholds, qualitatively determined

    if (photocellReading < 10) { Serial.println(" - Noir"); }

    else if (photocellReading < 200) { Serial.println(" - Sombre"); }

    else if (photocellReading < 500) { Serial.println(" - Lumiere"); }

    else if (photocellReading < 800) { Serial.println(" - Lumineux"); }

    else { Serial.println(" - Tres lumineux"); }

  

  /*----------------------------------------------------

   *                 XBEE SENSOR

   ---------------------------------------------------*/

    if (XBeeSerial.available()) {

      Serial.println(XBeeSerial.read());

    }

}
